# Fritzing sketch HC-06 (saved by Fritzing 0.9.9b)
circuit board: 8.46667cm x 5.64444cm

parts:
  Arduino_Uno_R3 = Arduino Uno (Rev3)
  HC-06 = Bluetooth HC-05 Macho

nets:
  N1: Arduino_Uno_R3.D2, HC-06.TXD
  N2: Arduino_Uno_R3.D3_PWM, HC-06.RXD
  N3: Arduino_Uno_R3.D4, HC-06.Key
  5V: Arduino_Uno_R3.5V, HC-06.VCC
  GND: Arduino_Uno_R3.GND, HC-06.GND
